// Logisim project LOGISIM-Project_Bueno-Perez.circ as structural Verilog: 26 circuits, main circuit main
module main (
  input  [3:0] in_1,
  input  [3:0] in_2,
  input  in_3,
  input  [1:0] Output
);

  wire [4:0] combination_of_adder_and_comparator_1_output;
  wire [6:0] base_selector_and_converter_1_out_3, base_selector_and_converter_1_out_4,
       base_selector_and_converter_1_out_5, base_selector_and_converter_1_out_6,
       base_selector_and_converter_1_out_7, base_selector_and_converter_1_out_8,
       base_selector_and_converter_1_out_9;

  Hex_Digit_Display hex_digit_display_1 (.value(in_1));  // open: dp
  Hex_Digit_Display hex_digit_display_2 (.value(in_2));  // open: dp
  Combination_of_Adder_and_Comparator combination_of_adder_and_comparator_1 (
    .in_1(in_1), .in_2(in_2), .in_3(in_3), .Output(combination_of_adder_and_comparator_1_output));
  Base_Selector_and_Converter base_selector_and_converter_1 (
    .in_1(combination_of_adder_and_comparator_1_output), .in_2(Output),
    .out_3(base_selector_and_converter_1_out_3), .out_4(base_selector_and_converter_1_out_4),
    .out_5(base_selector_and_converter_1_out_5), .out_6(base_selector_and_converter_1_out_6),
    .out_7(base_selector_and_converter_1_out_7), .out_8(base_selector_and_converter_1_out_8),
    .out_9(base_selector_and_converter_1_out_9));
  _7_Segment_Display u_7_segment_display_1 (
    .g(base_selector_and_converter_1_out_9[6]), .f(base_selector_and_converter_1_out_8[6]),
    .a(base_selector_and_converter_1_out_3[6]), .b(base_selector_and_converter_1_out_4[6]),
    .e(base_selector_and_converter_1_out_7[6]), .d(base_selector_and_converter_1_out_6[6]),
    .c(base_selector_and_converter_1_out_5[6]));  // open: dp
  _7_Segment_Display u_7_segment_display_2 (
    .g(base_selector_and_converter_1_out_9[5]), .f(base_selector_and_converter_1_out_8[5]),
    .a(base_selector_and_converter_1_out_3[5]), .b(base_selector_and_converter_1_out_4[5]),
    .e(base_selector_and_converter_1_out_7[5]), .d(base_selector_and_converter_1_out_6[5]),
    .c(base_selector_and_converter_1_out_5[5]));  // open: dp
  _7_Segment_Display u_7_segment_display_3 (
    .g(base_selector_and_converter_1_out_9[4]), .f(base_selector_and_converter_1_out_8[4]),
    .a(base_selector_and_converter_1_out_3[4]), .b(base_selector_and_converter_1_out_4[4]),
    .e(base_selector_and_converter_1_out_7[4]), .d(base_selector_and_converter_1_out_6[4]),
    .c(base_selector_and_converter_1_out_5[4]));  // open: dp
  _7_Segment_Display u_7_segment_display_4 (
    .g(base_selector_and_converter_1_out_9[3]), .f(base_selector_and_converter_1_out_8[3]),
    .a(base_selector_and_converter_1_out_3[3]), .b(base_selector_and_converter_1_out_4[3]),
    .e(base_selector_and_converter_1_out_7[3]), .d(base_selector_and_converter_1_out_6[3]),
    .c(base_selector_and_converter_1_out_5[3]));  // open: dp
  _7_Segment_Display u_7_segment_display_5 (
    .g(base_selector_and_converter_1_out_9[2]), .f(base_selector_and_converter_1_out_8[2]),
    .a(base_selector_and_converter_1_out_3[2]), .b(base_selector_and_converter_1_out_4[2]),
    .e(base_selector_and_converter_1_out_7[2]), .d(base_selector_and_converter_1_out_6[2]),
    .c(base_selector_and_converter_1_out_5[2]));  // open: dp
  _7_Segment_Display u_7_segment_display_6 (
    .g(base_selector_and_converter_1_out_9[1]), .f(base_selector_and_converter_1_out_8[1]),
    .a(base_selector_and_converter_1_out_3[1]), .b(base_selector_and_converter_1_out_4[1]),
    .e(base_selector_and_converter_1_out_7[1]), .d(base_selector_and_converter_1_out_6[1]),
    .c(base_selector_and_converter_1_out_5[1]));  // open: dp
  _7_Segment_Display u_7_segment_display_7 (
    .g(base_selector_and_converter_1_out_9[0]), .f(base_selector_and_converter_1_out_8[0]),
    .a(base_selector_and_converter_1_out_3[0]), .b(base_selector_and_converter_1_out_4[0]),
    .e(base_selector_and_converter_1_out_7[0]), .d(base_selector_and_converter_1_out_6[0]),
    .c(base_selector_and_converter_1_out_5[0]));  // open: dp

  // Notes on the sheet:
  //   Operand A 
  //   (in hex)
  //   Operand B
  //   (in hex)
  //   Adder /
  //   Comparator
  //   Operation
  //   Selector
  //   Base
  //   Converter
  //   Base
  //   Selector
  //   MSB
  //   LSB
endmodule

module Adder (
  input  [3:0] in_1,
  input  [3:0] Operand_B,
  output [4:0] out_3
);

  Adder_part #(.width(4)) adder_1 (.a(in_1), .b(Operand_B), .out(out_3[3:0]), .cin(1'b0), .cout(out_3[4]));

  // Notes on the sheet:
  //   Operand A
  //   Output from Adder
endmodule

module Comparator (
  input  [3:0] in_1,
  input  [3:0] in_2,
  output [4:0] out_3
);

  wire [2:0] comparator_1_gt;

  Comparator_part #(.width(4), .mode("unsigned")) comparator_1 (
    .a(in_1), .b(in_2), .gt(comparator_1_gt[0]), .eq(comparator_1_gt[1]), .lt(comparator_1_gt[2]));
  Multiplexer #(.select(3), .width(4), .enable("false")) multiplexer_1 (
    .in1(in_1), .in2(4'b0000), .in4(in_2), .out(out_3[3:0]), .sel(comparator_1_gt));  // open: in0, in3, in5, in6, in7

  assign out_3[4] = 1'b0;

  // Notes on the sheet:
  //   Operand A
  //   Operand B
  //   Output from Comparator
endmodule

module Combination_of_Adder_and_Comparator (
  input  [3:0] in_1,
  input  [3:0] in_2,
  input  in_3,
  output [4:0] Output
);

  wire [4:0] adder_1_out_3, comparator_1_out_3;

  Adder adder_1 (.in_1(in_1), .Operand_B(in_2), .out_3(adder_1_out_3));
  Comparator comparator_1 (.in_1(in_1), .in_2(in_2), .out_3(comparator_1_out_3));
  Multiplexer #(.width(5), .enable("false")) multiplexer_1 (
    .in0(adder_1_out_3), .in1(comparator_1_out_3), .out(Output), .sel(in_3));

  // Notes on the sheet:
  //   Operand A
  //   Operand B
  //   Comparator
  //   Adder
  //   Operation Selector
endmodule

module Base_Selector_and_Converter (
  input  [4:0] in_1,
  input  [1:0] in_2,
  output [6:0] out_3,
  output [6:0] out_4,
  output [6:0] out_5,
  output [6:0] out_6,
  output [6:0] out_7,
  output [6:0] out_8,
  output [6:0] out_9
);

  wire [6:0] binary_a_1_out_2, binary_b_1_out_1, binary_c_1_out_1, binary_d_1_out_2, binary_e_1_out_2,
       binary_f_1_out_2, binary_g_1_out_1, mystery_a_1_out_2, mystery_b_1_output, mystery_c_1_out_2,
       mystery_d_1_out_2, mystery_e_1_out_2, mystery_f_1_out_2, mystery_g_1_out_2, octal_a_1_out_2,
       octal_b_1_out_2, octal_c_1_out_2, octal_d_1_out_2, octal_e_1_out_2, octal_f_1_out_2, octal_g_1_out_2;

  Binary_A binary_a_1 (.Input(in_1), .out_2(binary_a_1_out_2));
  Octal_A octal_a_1 (.in_1(in_1), .out_2(octal_a_1_out_2));
  Mystery_A mystery_a_1 (.in_1(in_1), .out_2(mystery_a_1_out_2));
  Binary_B binary_b_1 (.out_1(binary_b_1_out_1));
  Octal_B octal_b_1 (.in_1(in_1), .out_2(octal_b_1_out_2));
  Mystery_B mystery_b_1 (.in_1(in_1), .Output(mystery_b_1_output));
  Binary_C binary_c_1 (.out_1(binary_c_1_out_1));
  Octal_C octal_c_1 (.Input(in_1), .out_2(octal_c_1_out_2));
  Mystery_C mystery_c_1 (.in_1(in_1), .out_2(mystery_c_1_out_2));
  Binary_D binary_d_1 (.Input(in_1), .out_2(binary_d_1_out_2));
  Octal_D octal_d_1 (.in_1(in_1), .out_2(octal_d_1_out_2));
  Mystery_D mystery_d_1 (.Input(in_1), .out_2(mystery_d_1_out_2));
  Binary_E binary_e_1 (.Input(in_1), .out_2(binary_e_1_out_2));
  Octal_E octal_e_1 (.in_1(in_1), .out_2(octal_e_1_out_2));
  Mystery_E mystery_e_1 (.in_1(in_1), .out_2(mystery_e_1_out_2));
  Binary_F binary_f_1 (.Input(in_1), .out_2(binary_f_1_out_2));
  Octal_F octal_f_1 (.in_1(in_1), .out_2(octal_f_1_out_2));
  Mystery_F mystery_f_1 (.Input(in_1), .out_2(mystery_f_1_out_2));
  Binary_G binary_g_1 (.out_1(binary_g_1_out_1));
  Octal_G octal_g_1 (.Input(in_1), .out_2(octal_g_1_out_2));
  Mystery_G mystery_g_1 (.Input(in_1), .out_2(mystery_g_1_out_2));
  Multiplexer #(.select(2), .width(7), .enable("false")) multiplexer_1 (
    .in0(binary_a_1_out_2), .in1(octal_a_1_out_2), .in2(mystery_a_1_out_2), .out(out_3), .sel(in_2));  // open: in3
  Multiplexer #(.select(2), .width(7), .enable("false")) multiplexer_2 (
    .in0(binary_b_1_out_1), .in1(octal_b_1_out_2), .in2(mystery_b_1_output), .out(out_4), .sel(in_2));  // open: in3
  Multiplexer #(.select(2), .width(7), .enable("false")) multiplexer_3 (
    .in0(binary_c_1_out_1), .in1(octal_c_1_out_2), .in2(mystery_c_1_out_2), .out(out_5), .sel(in_2));  // open: in3
  Multiplexer #(.select(2), .width(7), .enable("false")) multiplexer_4 (
    .in0(binary_d_1_out_2), .in1(octal_d_1_out_2), .in2(mystery_d_1_out_2), .out(out_6), .sel(in_2));  // open: in3
  Multiplexer #(.select(2), .width(7), .enable("false")) multiplexer_5 (
    .in0(binary_e_1_out_2), .in1(octal_e_1_out_2), .in2(mystery_e_1_out_2), .out(out_7), .sel(in_2));  // open: in3
  Multiplexer #(.select(2), .width(7), .enable("false")) multiplexer_6 (
    .in0(binary_f_1_out_2), .in1(octal_f_1_out_2), .in2(mystery_f_1_out_2), .out(out_8), .sel(in_2));  // open: in3
  Multiplexer #(.select(2), .width(7), .enable("false")) multiplexer_7 (
    .in0(binary_g_1_out_1), .in1(octal_g_1_out_2), .in2(mystery_g_1_out_2), .out(out_9), .sel(in_2));  // open: in3

  // Notes on the sheet:
  //   Input for Base Converter
  //   Output from Adder/Converter
endmodule

module Binary_A (
  input  [4:0] Input,
  output [6:0] out_2
);

  not not_1 (out_2[4], Input[4]);
  not not_2 (out_2[3], Input[3]);
  not not_3 (out_2[2], Input[2]);
  not not_4 (out_2[1], Input[1]);
  not not_5 (out_2[0], Input[0]);

  assign out_2[6:5] = 2'b11;

  // Notes on the sheet:
  //   A0
  //   A1
  //   A2
  //   A3
  //   A4
  //   A5
  //   A6
endmodule

module Binary_B (
  output [6:0] out_1
);


  assign out_1 = {7{1'b1}};

  // Notes on the sheet:
  //   B0
  //   B1
  //   B2
  //   B3
  //   B4
  //   B5
  //   B6
endmodule

module Binary_C (
  output [6:0] out_1
);


  assign out_1 = {7{1'b1}};

  // Notes on the sheet:
  //   C0
  //   C1
  //   C2
  //   C3
  //   C4
  //   C5
  //   C6
endmodule

module Binary_D (
  input  [4:0] Input,
  output [6:0] out_2
);

  not not_1 (out_2[4], Input[4]);
  not not_2 (out_2[3], Input[3]);
  not not_3 (out_2[2], Input[2]);
  not not_4 (out_2[1], Input[1]);
  not not_5 (out_2[0], Input[0]);

  assign out_2[6:5] = 2'b11;

  // Notes on the sheet:
  //   D0
  //   D1
  //   D2
  //   D3
  //   D4
  //   D5
  //   D5
endmodule

module Binary_E (
  input  [4:0] Input,
  output [6:0] out_2
);

  not not_1 (out_2[4], Input[4]);
  not not_2 (out_2[3], Input[3]);
  not not_3 (out_2[2], Input[2]);
  not not_4 (out_2[1], Input[1]);
  not not_5 (out_2[0], Input[0]);

  assign out_2[6:5] = 2'b11;

  // Notes on the sheet:
  //   E1
  //   E3
  //   E4
  //   E5
  //   E6
  //   E7
  //   E2
endmodule

module Binary_F (
  input  [4:0] Input,
  output [6:0] out_2
);

  not not_1 (out_2[4], Input[4]);
  not not_2 (out_2[3], Input[3]);
  not not_3 (out_2[2], Input[2]);
  not not_4 (out_2[1], Input[1]);
  not not_5 (out_2[0], Input[0]);

  assign out_2[6:5] = 2'b11;
endmodule

module Binary_G (
  output [6:0] out_1
);


  assign out_1 = {7{1'b0}};

  // Notes on the sheet:
  //   G0
  //   G1
  //   G2
  //   G3
  //   G5
  //   G6
  //   G4
endmodule

module Octal_A (
  input  [4:0] in_1,
  output [6:0] out_2
);

  wire and_1_out, and_2_out, not_1_out, not_2_out, not_3_out;

  not not_1 (not_1_out, in_1[3]);
  not not_2 (not_2_out, in_1[2]);
  not not_3 (not_3_out, in_1[0]);
  or or_1 (out_2[1], not_1_out, in_1[4]);
  and and_1 (and_1_out, not_2_out, not_3_out);
  and and_2 (and_2_out, in_1[2], in_1[0]);
  or or_2 (out_2[0], and_1_out, in_1[1], and_2_out);

  assign out_2[6:2] = {5{1'b1}};

  // Notes on the sheet:
  //   Input
  //   A0
  //   A1
  //   A2
  //   A3
  //   A4
  //   A5
  //   A6
endmodule

module Octal_B (
  input  [4:0] in_1,
  output [6:0] out_2
);

  wire and_1_out, and_2_out, not_1_out, not_2_out, not_3_out;

  not not_1 (not_1_out, in_1[1]);
  not not_2 (not_2_out, in_1[0]);
  not not_3 (not_3_out, in_1[2]);
  and and_1 (and_1_out, not_1_out, not_2_out);
  and and_2 (and_2_out, in_1[1], in_1[0]);
  or or_1 (out_2[0], not_3_out, and_1_out, and_2_out);

  assign out_2[6:1] = {6{1'b1}};

  // Notes on the sheet:
  //   Input
  //   B0
  //   B1
  //   B2
  //   B3
  //   B4
  //   B5
  //   B6
endmodule

module Octal_C (
  input  [4:0] Input,
  output [6:0] out_2
);

  wire not_1_out, not_2_out;

  not not_1 (not_1_out, Input[4]);
  not not_2 (not_2_out, Input[1]);
  or or_1 (out_2[1], not_1_out, Input[3]);
  or or_2 (out_2[0], not_2_out, Input[0], Input[2]);

  assign out_2[6:2] = {5{1'b1}};

  // Notes on the sheet:
  //   C0
  //   C1
  //   C2
  //   C3
  //   C4
  //   C5
  //   C6
endmodule

module Octal_D (
  input  [4:0] in_1,
  output [6:0] out_2
);

  wire and_1_out, and_2_out, and_3_out, and_4_out, not_1_out, not_2_out, not_3_out, not_4_out, not_5_out,
       not_6_out;

  not not_1 (not_1_out, in_1[3]);
  not not_2 (not_2_out, in_1[2]);
  not not_3 (not_3_out, in_1[0]);
  not not_4 (not_4_out, in_1[2]);
  not not_5 (not_5_out, in_1[0]);
  not not_6 (not_6_out, in_1[1]);
  or or_1 (out_2[1], not_1_out, in_1[4]);
  and and_1 (and_1_out, not_2_out, not_3_out);
  and and_2 (and_2_out, not_4_out, in_1[1]);
  and and_3 (and_3_out, in_1[1], not_5_out);
  and and_4 (and_4_out, in_1[2], not_6_out, in_1[0]);
  or or_2 (out_2[0], and_1_out, and_2_out, and_3_out, and_4_out);

  assign out_2[6:2] = {5{1'b1}};

  // Notes on the sheet:
  //   Input
  //   D0
  //   D1
  //   D2
  //   D3
  //   D4
  //   D5
  //   D6
endmodule

module Octal_E (
  input  [4:0] in_1,
  output [6:0] out_2
);

  wire and_1_out, and_2_out, not_2_out, not_3_out, not_4_out;

  not not_1 (out_2[1], in_1[3]);
  not not_2 (not_2_out, in_1[2]);
  and and_1 (and_1_out, not_2_out, not_3_out);
  not not_3 (not_3_out, in_1[0]);
  and and_2 (and_2_out, in_1[1], not_4_out);
  not not_4 (not_4_out, in_1[0]);
  or or_1 (out_2[0], and_1_out, and_2_out);

  assign out_2[6:2] = {5{1'b1}};

  // Notes on the sheet:
  //   Input
  //   E0
  //   E1
  //   E2
  //   E3
  //   E4
  //   E5
  //   E6
endmodule

module Octal_F (
  input  [4:0] in_1,
  output [6:0] out_2
);

  wire and_2_out, and_3_out, and_4_out, not_1_out, not_2_out, not_3_out, not_4_out, not_5_out, not_6_out;

  not not_1 (not_1_out, in_1[4]);
  not not_2 (not_2_out, in_1[3]);
  not not_3 (not_3_out, in_1[1]);
  not not_4 (not_4_out, in_1[0]);
  not not_5 (not_5_out, in_1[1]);
  not not_6 (not_6_out, in_1[0]);
  and and_1 (out_2[1], not_1_out, not_2_out);
  and and_2 (and_2_out, not_3_out, not_4_out);
  and and_3 (and_3_out, in_1[2], not_5_out);
  and and_4 (and_4_out, in_1[2], not_6_out);
  or or_1 (out_2[0], and_2_out, and_3_out, and_4_out);

  assign out_2[6:2] = {5{1'b1}};

  // Notes on the sheet:
  //   Input
  //   F0
  //   F1
  //   F2
  //   F3
  //   F4
  //   F5
  //   F6
endmodule

module Octal_G (
  input  [4:0] Input,
  output [6:0] out_2
);

  wire and_1_out, and_2_out, and_3_out, not_1_out, not_2_out, not_3_out;

  not not_1 (not_1_out, Input[2]);
  not not_2 (not_2_out, Input[1]);
  not not_3 (not_3_out, Input[0]);
  and and_1 (and_1_out, not_1_out, Input[1]);
  and and_2 (and_2_out, Input[2], not_2_out);
  and and_3 (and_3_out, Input[2], not_3_out);
  or or_1 (out_2[0], and_1_out, and_2_out, and_3_out);

  assign out_2[6:1] = {{5{1'b0}}, Input[4]};

  // Notes on the sheet:
  //   G0
  //   G1
  //   G2
  //   G3
  //   G4
  //   G5
  //   G6
endmodule

module Mystery_A (
  input  [4:0] in_1,
  output [6:0] out_2
);

  wire and_1_out, and_2_out, and_3_out, and_4_out, and_5_out, and_6_out, not_1_out, not_2_out, not_3_out,
       not_4_out, not_5_out, not_6_out, not_7_out, not_8_out, not_9_out, not_10_out, not_11_out, not_12_out,
       not_13_out, not_14_out, not_15_out, not_16_out, not_17_out, not_18_out, not_19_out, not_20_out,
       or_1_out, or_2_out, or_3_out, or_4_out, or_5_out, or_6_out;

  not not_1 (not_1_out, in_1[3]);
  not not_2 (not_2_out, in_1[2]);
  not not_3 (not_3_out, in_1[3]);
  not not_4 (not_4_out, in_1[1]);
  not not_5 (not_5_out, in_1[4]);
  not not_6 (not_6_out, in_1[3]);
  not not_7 (not_7_out, in_1[2]);
  not not_8 (not_8_out, in_1[4]);
  not not_9 (not_9_out, in_1[0]);
  not not_10 (not_10_out, in_1[0]);
  not not_11 (not_11_out, in_1[2]);
  not not_12 (not_12_out, in_1[3]);
  not not_13 (not_13_out, in_1[3]);
  not not_14 (not_14_out, in_1[1]);
  not not_15 (not_15_out, in_1[0]);
  not not_16 (not_16_out, in_1[4]);
  not not_17 (not_17_out, in_1[1]);
  not not_18 (not_18_out, in_1[4]);
  not not_19 (not_19_out, in_1[3]);
  not not_20 (not_20_out, in_1[0]);
  and and_1 (and_1_out, not_1_out, not_2_out);
  and and_2 (and_2_out, not_3_out, not_4_out);
  and and_3 (and_3_out, not_5_out, in_1[3], in_1[2], in_1[1]);
  and and_4 (and_4_out, in_1[4], not_6_out);
  and and_5 (and_5_out, in_1[4], not_7_out);
  and and_6 (and_6_out, not_8_out, in_1[2], in_1[1], not_9_out);
  or or_1 (or_1_out, in_1[4], in_1[3], in_1[2], in_1[1], not_10_out);
  or or_2 (or_2_out, in_1[4], in_1[3], not_11_out, in_1[1], in_1[0]);
  or or_3 (or_3_out, in_1[4], not_12_out, in_1[2], in_1[1], in_1[0]);
  or or_4 (or_4_out, in_1[4], not_13_out, not_14_out, not_15_out);
  or or_5 (or_5_out, not_16_out, in_1[3], not_17_out, in_1[0]);
  or or_6 (or_6_out, not_18_out, not_19_out, in_1[1], not_20_out);
  or or_7 (out_2[1], and_1_out, and_2_out, and_3_out, and_4_out, and_5_out, and_6_out);
  and and_7 (out_2[0], or_1_out, or_2_out, or_3_out, or_4_out, or_5_out, or_6_out);

  assign out_2[6:2] = {5{1'b1}};

  // Notes on the sheet:
  //   A0
  //   A1
  //   A2
  //   A3
  //   A4
  //   A5
  //   A6
endmodule

module Mystery_B (
  input  [4:0] in_1,
  output [6:0] Output
);

  wire not_1_out, not_2_out, not_3_out, not_4_out, not_5_out, not_6_out, not_7_out, not_8_out, not_9_out,
       not_10_out, not_11_out, not_12_out, not_13_out, not_14_out, or_1_out, or_2_out, or_3_out, or_4_out,
       or_5_out, or_6_out;

  not not_1 (not_1_out, in_1[2]);
  not not_2 (not_2_out, in_1[0]);
  not not_3 (not_3_out, in_1[2]);
  not not_4 (not_4_out, in_1[1]);
  not not_5 (not_5_out, in_1[3]);
  not not_6 (not_6_out, in_1[2]);
  not not_7 (not_7_out, in_1[4]);
  not not_8 (not_8_out, in_1[1]);
  not not_9 (not_9_out, in_1[0]);
  not not_10 (not_10_out, in_1[4]);
  not not_11 (not_11_out, in_1[2]);
  not not_12 (not_12_out, in_1[4]);
  not not_13 (not_13_out, in_1[3]);
  not not_14 (not_14_out, in_1[1]);
  or or_1 (or_1_out, in_1[4], not_1_out, in_1[1], not_2_out);
  or or_2 (or_2_out, in_1[4], in_1[3], not_3_out, not_4_out, in_1[0]);
  or or_3 (or_3_out, in_1[4], not_5_out, not_6_out, in_1[1]);
  or or_4 (or_4_out, not_7_out, in_1[2], not_8_out, not_9_out);
  or or_5 (or_5_out, not_10_out, in_1[3], not_11_out, in_1[1], in_1[0]);
  or or_6 (or_6_out, not_12_out, not_13_out, in_1[2], not_14_out);
  and and_1 (Output[0], or_1_out, or_2_out, or_3_out, or_4_out, or_5_out, or_6_out);

  assign Output[6:1] = {6{1'b1}};

  // Notes on the sheet:
  //   B0
  //   B1
  //   B2
  //   B3
  //   B4
  //   B5
  //   B6
endmodule

module Mystery_C (
  input  [4:0] in_1,
  output [6:0] out_2
);

  wire and_1_out, and_2_out, and_3_out, and_4_out, and_5_out, not_1_out, not_2_out, not_3_out, not_4_out,
       not_5_out, not_6_out, not_7_out, not_8_out, not_9_out, not_10_out, not_11_out, not_12_out, not_13_out,
       not_14_out, not_15_out, not_16_out, not_17_out, or_1_out, or_2_out, or_3_out, or_4_out, or_5_out;

  not not_1 (not_1_out, in_1[4]);
  not not_2 (not_2_out, in_1[3]);
  not not_3 (not_3_out, in_1[2]);
  not not_4 (not_4_out, in_1[1]);
  not not_5 (not_5_out, in_1[1]);
  not not_6 (not_6_out, in_1[1]);
  not not_7 (not_7_out, in_1[3]);
  not not_8 (not_8_out, in_1[0]);
  not not_9 (not_9_out, in_1[4]);
  not not_10 (not_10_out, in_1[4]);
  not not_11 (not_11_out, in_1[2]);
  not not_12 (not_12_out, in_1[1]);
  not not_13 (not_13_out, in_1[0]);
  not not_14 (not_14_out, in_1[4]);
  not not_15 (not_15_out, in_1[3]);
  not not_16 (not_16_out, in_1[2]);
  not not_17 (not_17_out, in_1[1]);
  and and_1 (and_1_out, not_1_out, not_2_out);
  and and_2 (and_2_out, in_1[3], not_3_out);
  and and_3 (and_3_out, in_1[3], not_4_out);
  and and_4 (and_4_out, in_1[2], not_5_out, in_1[0]);
  and and_5 (and_5_out, in_1[4], in_1[2], in_1[1]);
  or or_1 (or_1_out, in_1[4], in_1[3], in_1[2], not_6_out, in_1[0]);
  or or_2 (or_2_out, in_1[4], not_7_out, in_1[2], in_1[1], not_8_out);
  or or_3 (or_3_out, not_9_out, in_1[3], in_1[2], in_1[1], in_1[0]);
  or or_4 (or_4_out, not_10_out, not_11_out, not_12_out, not_13_out);
  or or_5 (or_5_out, not_14_out, not_15_out, not_16_out, not_17_out);
  or or_6 (out_2[1], and_1_out, and_2_out, and_3_out, and_4_out, and_5_out);
  and and_6 (out_2[0], or_1_out, or_2_out, or_3_out, or_4_out, or_5_out);

  assign out_2[6:2] = {5{1'b1}};

  // Notes on the sheet:
  //   C0
  //   C1
  //   C2
  //   C3
  //   C4
  //   C5
  //   C6
endmodule

module Mystery_D (
  input  [4:0] Input,
  output [6:0] out_2
);

  wire not_1_out, not_2_out, not_3_out, not_4_out, not_5_out, not_6_out, not_7_out, not_8_out, not_9_out,
       not_10_out, not_11_out, not_12_out, not_13_out, not_14_out, not_15_out, not_16_out, not_17_out,
       not_18_out, not_19_out, not_20_out, or_1_out, or_2_out, or_3_out, or_4_out, or_5_out, or_6_out,
       or_7_out, or_8_out, or_9_out, or_10_out;

  not not_1 (not_1_out, Input[2]);
  not not_2 (not_2_out, Input[1]);
  not not_3 (not_3_out, Input[0]);
  not not_4 (not_4_out, Input[3]);
  not not_5 (not_5_out, Input[4]);
  not not_6 (not_6_out, Input[3]);
  not not_7 (not_7_out, Input[2]);
  not not_8 (not_8_out, Input[3]);
  not not_9 (not_9_out, Input[2]);
  not not_10 (not_10_out, Input[0]);
  not not_11 (not_11_out, Input[2]);
  not not_12 (not_12_out, Input[3]);
  not not_13 (not_13_out, Input[3]);
  not not_14 (not_14_out, Input[1]);
  not not_15 (not_15_out, Input[0]);
  not not_16 (not_16_out, Input[4]);
  not not_17 (not_17_out, Input[1]);
  not not_18 (not_18_out, Input[4]);
  not not_19 (not_19_out, Input[3]);
  not not_20 (not_20_out, Input[0]);
  or or_1 (or_1_out, Input[4], Input[3], not_1_out, not_2_out, not_3_out);
  or or_2 (or_2_out, Input[4], not_4_out, Input[2]);
  or or_3 (or_3_out, not_5_out, not_6_out, not_7_out);
  or or_4 (or_4_out, not_8_out, not_9_out, Input[1]);
  or or_5 (or_5_out, Input[4], Input[3], Input[2], Input[1], not_10_out);
  or or_6 (or_6_out, Input[4], Input[3], not_11_out, Input[1], Input[0]);
  or or_7 (or_7_out, Input[4], not_12_out, Input[2], Input[1], Input[0]);
  or or_8 (or_8_out, Input[4], not_13_out, not_14_out, not_15_out);
  or or_9 (or_9_out, not_16_out, Input[3], not_17_out, Input[0]);
  or or_10 (or_10_out, not_18_out, not_19_out, Input[1], not_20_out);
  and and_1 (out_2[1], or_1_out, or_2_out, or_3_out, or_4_out);
  and and_2 (out_2[0], or_5_out, or_6_out, or_7_out, or_8_out, or_9_out, or_10_out);

  assign out_2[6:2] = {5{1'b1}};

  // Notes on the sheet:
  //   D0
  //   D1
  //   D2
  //   D3
  //   D4
  //   D5
  //   D6
endmodule

module Mystery_E (
  input  [4:0] in_1,
  output [6:0] out_2
);

  wire and_1_out, and_2_out, and_3_out, and_4_out, and_5_out, and_6_out, and_7_out, and_8_out, and_9_out,
       and_10_out, and_11_out, and_12_out, and_13_out, not_1_out, not_2_out, not_3_out, not_4_out, not_5_out,
       not_6_out, not_7_out, not_8_out, not_9_out, not_10_out, not_11_out, not_12_out, not_13_out,
       not_14_out, not_15_out, not_16_out, not_17_out, not_18_out, not_19_out, not_20_out, not_21_out,
       not_22_out, not_23_out, not_24_out, not_25_out, not_26_out;

  not not_1 (not_1_out, in_1[4]);
  not not_2 (not_2_out, in_1[3]);
  not not_3 (not_3_out, in_1[1]);
  not not_4 (not_4_out, in_1[3]);
  not not_5 (not_5_out, in_1[2]);
  not not_6 (not_6_out, in_1[3]);
  not not_7 (not_7_out, in_1[1]);
  not not_8 (not_8_out, in_1[0]);
  not not_9 (not_9_out, in_1[4]);
  not not_10 (not_10_out, in_1[0]);
  not not_11 (not_11_out, in_1[4]);
  not not_12 (not_12_out, in_1[4]);
  not not_13 (not_13_out, in_1[3]);
  not not_14 (not_14_out, in_1[2]);
  not not_15 (not_15_out, in_1[0]);
  not not_16 (not_16_out, in_1[4]);
  not not_17 (not_17_out, in_1[3]);
  not not_18 (not_18_out, in_1[4]);
  not not_19 (not_19_out, in_1[0]);
  not not_20 (not_20_out, in_1[4]);
  not not_21 (not_21_out, in_1[1]);
  not not_22 (not_22_out, in_1[3]);
  not not_23 (not_23_out, in_1[1]);
  not not_24 (not_24_out, in_1[0]);
  not not_25 (not_25_out, in_1[3]);
  not not_26 (not_26_out, in_1[0]);
  and and_1 (and_1_out, not_1_out, not_2_out, not_3_out);
  and and_2 (and_2_out, not_4_out, not_5_out);
  and and_3 (and_3_out, not_6_out, not_7_out, not_8_out);
  and and_4 (and_4_out, not_9_out, in_1[2], in_1[1], not_10_out);
  and and_5 (and_5_out, not_11_out, in_1[3], in_1[2], in_1[1]);
  and and_6 (and_6_out, not_12_out, not_13_out, not_14_out, not_15_out);
  and and_7 (and_7_out, not_16_out, not_17_out, in_1[2], in_1[1]);
  and and_8 (and_8_out, not_18_out, in_1[2], in_1[1], not_19_out);
  and and_9 (and_9_out, not_20_out, in_1[3], not_21_out, in_1[0]);
  and and_10 (and_10_out, in_1[4], not_22_out, not_23_out, not_24_out);
  and and_11 (and_11_out, in_1[4], not_25_out, in_1[2], in_1[0]);
  and and_12 (and_12_out, in_1[4], in_1[3], in_1[1], in_1[0]);
  and and_13 (and_13_out, in_1[4], in_1[3], in_1[2], not_26_out);
  or or_1 (out_2[1], and_1_out, and_2_out, and_3_out, and_4_out, and_5_out);
  or or_2 (out_2[0], and_6_out, and_7_out, and_8_out, and_9_out, and_10_out, and_11_out, and_12_out, and_13_out);

  assign out_2[6:2] = {5{1'b1}};

  // Notes on the sheet:
  //   Input
  //   E0
  //   E1
  //   E2
  //   E3
  //   E4
  //   E5
  //   E6
endmodule

module Mystery_F (
  input  [4:0] Input,
  output [6:0] out_2
);

  wire and_1_out, and_2_out, and_3_out, and_4_out, and_5_out, and_6_out, and_7_out, and_8_out, and_9_out,
       and_10_out, and_11_out, and_12_out, and_13_out, not_1_out, not_2_out, not_3_out, not_4_out, not_5_out,
       not_6_out, not_7_out, not_8_out, not_9_out, not_10_out, not_11_out, not_12_out, not_13_out,
       not_14_out, not_15_out, not_16_out, not_17_out, not_18_out, not_19_out, not_20_out, not_21_out,
       not_22_out, not_23_out, not_24_out, not_25_out, not_26_out;

  not not_1 (not_1_out, Input[4]);
  not not_2 (not_2_out, Input[3]);
  not not_3 (not_3_out, Input[2]);
  not not_4 (not_4_out, Input[4]);
  not not_5 (not_5_out, Input[3]);
  not not_6 (not_6_out, Input[1]);
  not not_7 (not_7_out, Input[4]);
  not not_8 (not_8_out, Input[3]);
  not not_9 (not_9_out, Input[0]);
  not not_10 (not_10_out, Input[4]);
  not not_11 (not_11_out, Input[3]);
  not not_12 (not_12_out, Input[1]);
  not not_13 (not_13_out, Input[0]);
  not not_14 (not_14_out, Input[4]);
  not not_15 (not_15_out, Input[3]);
  not not_16 (not_16_out, Input[4]);
  not not_17 (not_17_out, Input[1]);
  not not_18 (not_18_out, Input[4]);
  not not_19 (not_19_out, Input[0]);
  not not_20 (not_20_out, Input[3]);
  not not_21 (not_21_out, Input[1]);
  not not_22 (not_22_out, Input[1]);
  not not_23 (not_23_out, Input[0]);
  not not_24 (not_24_out, Input[2]);
  not not_25 (not_25_out, Input[2]);
  not not_26 (not_26_out, Input[2]);
  and and_1 (and_1_out, not_1_out, not_2_out, not_3_out);
  and and_2 (and_2_out, not_4_out, not_5_out, not_6_out);
  and and_3 (and_3_out, not_7_out, not_8_out, not_9_out);
  and and_4 (and_4_out, Input[4], Input[3], Input[2]);
  and and_5 (and_5_out, not_10_out, not_11_out, not_12_out, not_13_out);
  and and_6 (and_6_out, not_14_out, not_15_out, Input[2]);
  and and_7 (and_7_out, not_16_out, Input[2], not_17_out);
  and and_8 (and_8_out, not_18_out, Input[2], not_19_out);
  and and_9 (and_9_out, not_20_out, Input[2], not_21_out);
  and and_10 (and_10_out, Input[2], not_22_out, not_23_out);
  and and_11 (and_11_out, Input[3], not_24_out, Input[1], Input[0]);
  and and_12 (and_12_out, Input[4], not_25_out, Input[1]);
  and and_13 (and_13_out, Input[4], Input[3], not_26_out, Input[0]);
  or or_1 (out_2[1], and_1_out, and_2_out, and_3_out, and_4_out);
  or or_2 (out_2[0], and_5_out, and_6_out, and_7_out, and_8_out, and_9_out, and_10_out, and_11_out, and_12_out, and_13_out);

  assign out_2[6:2] = {5{1'b1}};

  // Notes on the sheet:
  //   F0
  //   F1
  //   F2
  //   F3
  //   F4
  //   F5
  //   F6
endmodule

module Mystery_G (
  input  [4:0] Input,
  output [6:0] out_2
);

  wire and_1_out, not_1_out, not_2_out, not_3_out, not_4_out, not_5_out, not_6_out, not_7_out, not_8_out,
       not_9_out, not_10_out, not_11_out, not_12_out, not_13_out, not_14_out, not_15_out, or_2_out, or_3_out,
       or_4_out, or_5_out, or_6_out, or_7_out, or_8_out;

  and and_1 (and_1_out, Input[3], Input[2], Input[1]);
  not not_1 (not_1_out, Input[2]);
  not not_2 (not_2_out, Input[1]);
  not not_3 (not_3_out, Input[0]);
  not not_4 (not_4_out, Input[3]);
  not not_5 (not_5_out, Input[2]);
  not not_6 (not_6_out, Input[1]);
  not not_7 (not_7_out, Input[4]);
  not not_8 (not_8_out, Input[2]);
  not not_9 (not_9_out, Input[0]);
  not not_10 (not_10_out, Input[4]);
  not not_11 (not_11_out, Input[2]);
  not not_12 (not_12_out, Input[1]);
  not not_13 (not_13_out, Input[4]);
  not not_14 (not_14_out, Input[3]);
  not not_15 (not_15_out, Input[2]);
  or or_1 (out_2[1], and_1_out, Input[4]);
  or or_2 (or_2_out, Input[4], Input[3], Input[2], Input[1]);
  or or_3 (or_3_out, Input[4], not_1_out, not_2_out, not_3_out);
  or or_4 (or_4_out, Input[4], Input[2], Input[1], Input[0]);
  or or_5 (or_5_out, Input[4], not_4_out, not_5_out, not_6_out);
  or or_6 (or_6_out, not_7_out, not_8_out, Input[1], not_9_out);
  or or_7 (or_7_out, not_10_out, Input[3], not_11_out, not_12_out, Input[0]);
  or or_8 (or_8_out, not_13_out, not_14_out, not_15_out, Input[1]);
  and and_2 (out_2[0], or_2_out, or_3_out, or_4_out, or_5_out, or_6_out, or_7_out, or_8_out);

  assign out_2[6:2] = {5{1'b0}};

  // Notes on the sheet:
  //   G0
  //   G1
  //   G2
  //   G3
  //   G4
  //   G5
  //   G6
endmodule
